// Logisim project control-logic.circ as structural Verilog: 1 circuit, main circuit control_logic
module control_logic (
  input  [31:0] Instruction,
  input  BrEq,
  input  BrLt,
  output PCSel,
  output RegWEn,
  output [2:0] ImmSel,
  output BrUn,
  output ASel,
  output BSel,
  output [3:0] ALUSel,
  output MemWEn,
  output [1:0] WBSel
);

  wire add0, addi0, and0, and_6_out, and_17_out, and_18_out, and_19_out, and_20_out, and_21_out, and_22_out,
       and_23_out, and_24_out, and_28_out, and_33_out, and_41_out, andi0, auipc0, beq0, bge0, bgeu0, blt0,
       bltu0, bne0, comparator_3_eq, comparator_5_eq, comparator_6_eq, comparator_7_eq, comparator_8_eq,
       comparator_9_eq, comparator_10_eq, comparator_11_eq, comparator_12_eq, comparator_13_eq,
       comparator_14_eq, comparator_15_eq, comparator_16_eq, comparator_17_eq, comparator_18_eq,
       comparator_19_eq, comparator_20_eq, jal0, jalr0, lb0, lh0, lui0, lw0, mul0, mulh0, mulhu0, not_1_out,
       not_2_out, not_3_out, or0, ori0, sb0, sh0, sll0, slli0, slt0, slti0, sra0, srai0, srl0, srli0, sub0,
       sw0, xor0, xori0;
  wire [5:0] priority_encoder_1_out;
  wire [15:14] rom_1_data;

  Priority_Encoder #(.select_enc(6)) priority_encoder_1 (
    .in0(add0), .in1(mul0), .in2(sub0), .in3(sll0), .in4(mulh0), .in5(mulhu0), .in6(slt0), .in7(xor0),
    .in8(srl0), .in9(sra0), .in10(or0), .in11(and0), .in12(lb0), .in13(lh0), .in14(lw0), .in15(addi0),
    .in16(slli0), .in17(slti0), .in18(xori0), .in19(srli0), .in20(srai0), .in21(ori0), .in22(andi0),
    .in23(sb0), .in24(sh0), .in25(sw0), .in26(beq0), .in27(bne0), .in28(blt0), .in29(bge0), .in30(bltu0),
    .in31(bgeu0), .in32(auipc0), .in33(lui0), .in34(jal0), .in35(jalr0), .out(priority_encoder_1_out));  // open: in36, in37, in38, in39, in40, in41, in42, in43, in44, in45, in46, in47, in48, in49, in50, in51, in52, in53, in54, in55, in56, in57, in58, in59, in60, in61, in62, in63, gs, en_out, en_in
  ROM #(.addrWidth(6), .dataWidth(16)) rom_1 (
    .addr(priority_encoder_1_out),
    .data({rom_1_data, WBSel, MemWEn, ALUSel, BSel, ASel, BrUn, ImmSel, RegWEn}));
  Comparator #(.width(7)) comparator_1 (.a(7'b0110111), .b(Instruction[6:0]), .eq(lui0));  // open: gt, lt
  Comparator #(.width(7)) comparator_2 (.a(7'b0010111), .b(Instruction[6:0]), .eq(auipc0));  // open: gt, lt
  Comparator #(.width(7)) comparator_3 (.a(7'b1100111), .b(Instruction[6:0]), .eq(comparator_3_eq));  // open: gt, lt
  Comparator #(.width(7)) comparator_4 (.a(7'b1101111), .b(Instruction[6:0]), .eq(jal0));  // open: gt, lt
  Comparator #(.width(7)) comparator_5 (.a(7'b0100011), .b(Instruction[6:0]), .eq(comparator_5_eq));  // open: gt, lt
  Comparator #(.width(7)) comparator_6 (.a(7'b0000011), .b(Instruction[6:0]), .eq(comparator_6_eq));  // open: gt, lt
  Comparator #(.width(7)) comparator_7 (.a(7'b1100011), .b(Instruction[6:0]), .eq(comparator_7_eq));  // open: gt, lt
  Comparator #(.width(7)) comparator_8 (.a(7'b0010011), .b(Instruction[6:0]), .eq(comparator_8_eq));  // open: gt, lt
  Comparator #(.width(7)) comparator_9 (.a(Instruction[6:0]), .b(7'b0110011), .eq(comparator_9_eq));  // open: gt, lt
  Comparator #(.width(3)) comparator_10 (.a(3'b000), .b(Instruction[14:12]), .eq(comparator_10_eq));  // open: gt, lt
  and and_1 (jalr0, comparator_10_eq, comparator_3_eq);
  and and_2 (sb0, comparator_5_eq, comparator_10_eq);
  and and_3 (lb0, comparator_6_eq, comparator_10_eq);
  and and_4 (beq0, comparator_7_eq, comparator_10_eq);
  and and_5 (addi0, comparator_10_eq, comparator_8_eq);
  and and_6 (and_6_out, comparator_10_eq, comparator_9_eq);
  Comparator #(.width(3)) comparator_11 (.a(3'b001), .b(Instruction[14:12]), .eq(comparator_11_eq));  // open: gt, lt
  Comparator #(.width(7)) comparator_12 (
    .a(7'b0000001), .b(Instruction[31:25]), .eq(comparator_12_eq));  // open: gt, lt
  and and_7 (sh0, comparator_5_eq, comparator_11_eq);
  and and_8 (lh0, comparator_6_eq, comparator_11_eq);
  and and_9 (bne0, comparator_11_eq, comparator_7_eq);
  and and_10 (slli0, comparator_11_eq, comparator_8_eq);
  and and_11 (mul0, and_6_out, comparator_12_eq);
  and and_12 (add0, and_6_out, comparator_14_eq);
  and and_13 (sub0, and_6_out, comparator_16_eq);
  Comparator #(.width(3)) comparator_13 (.a(3'b010), .b(Instruction[14:12]), .eq(comparator_13_eq));  // open: gt, lt
  Comparator #(.width(7)) comparator_14 (.a({7{1'b0}}), .b(Instruction[31:25]), .eq(comparator_14_eq));  // open: gt, lt
  not not_1 (not_1_out, BrEq);
  not not_2 (not_2_out, BrLt);
  not not_3 (not_3_out, BrLt);
  and and_14 (sw0, comparator_5_eq, comparator_13_eq);
  and and_15 (lw0, comparator_6_eq, comparator_13_eq);
  and and_16 (slti0, comparator_13_eq, comparator_8_eq);
  Comparator #(.width(3)) comparator_15 (.a(3'b011), .b(Instruction[14:12]), .eq(comparator_15_eq));  // open: gt, lt
  and and_17 (and_17_out, comparator_11_eq, comparator_9_eq);
  and and_18 (and_18_out, comparator_9_eq, comparator_15_eq);
  and and_19 (and_19_out, BrEq, beq0);
  and and_20 (and_20_out, not_1_out, bne0);
  and and_21 (and_21_out, BrLt, blt0);
  and and_22 (and_22_out, not_2_out, bge0);
  and and_23 (and_23_out, BrLt, bltu0);
  and and_24 (and_24_out, not_3_out, bgeu0);
  // AND_Gate and_25 has open pins: in0=comparator_15_eq, in1=comparator_8_eq, out=open
  Comparator #(.width(7)) comparator_16 (
    .a(7'b0100000), .b(Instruction[31:25]), .eq(comparator_16_eq));  // open: gt, lt
  and and_26 (sll0, and_17_out, comparator_14_eq);
  and and_27 (mulhu0, and_18_out, comparator_12_eq);
  Comparator #(.width(3)) comparator_17 (.a(3'b100), .b(Instruction[14:12]), .eq(comparator_17_eq));  // open: gt, lt
  and and_28 (and_28_out, comparator_11_eq, comparator_9_eq);
  or or_1 (PCSel, jal0, and_19_out, and_20_out, and_21_out, and_22_out, and_23_out, and_24_out, jalr0);
  and and_29 (blt0, comparator_17_eq, comparator_7_eq);
  and and_30 (xori0, comparator_17_eq, comparator_8_eq);
  Comparator #(.width(3)) comparator_18 (.a(3'b101), .b(Instruction[14:12]), .eq(comparator_18_eq));  // open: gt, lt
  and and_31 (slt0, comparator_13_eq, comparator_9_eq);
  and and_32 (mulh0, and_28_out, comparator_12_eq);
  and and_33 (and_33_out, comparator_18_eq, comparator_8_eq);
  and and_34 (bge0, comparator_18_eq, comparator_7_eq);
  and and_35 (srli0, comparator_14_eq, and_33_out);
  and and_36 (srai0, comparator_16_eq, and_33_out);
  Comparator #(.width(3)) comparator_19 (.a(3'b110), .b(Instruction[14:12]), .eq(comparator_19_eq));  // open: gt, lt
  and and_37 (xor0, comparator_17_eq, comparator_9_eq);
  and and_38 (ori0, comparator_19_eq, comparator_8_eq);
  Comparator #(.width(3)) comparator_20 (.a(3'b111), .b(Instruction[14:12]), .eq(comparator_20_eq));  // open: gt, lt
  and and_39 (bltu0, comparator_7_eq, comparator_19_eq);
  and and_40 (andi0, comparator_20_eq, comparator_8_eq);
  and and_41 (and_41_out, comparator_18_eq, comparator_9_eq);
  and and_42 (sra0, and_41_out, comparator_18_eq);
  and and_43 (srl0, and_41_out, comparator_14_eq);
  and and_44 (bgeu0, comparator_7_eq, comparator_20_eq);
  and and_45 (or0, comparator_19_eq, comparator_9_eq);
  and and_46 (and0, comparator_9_eq, comparator_20_eq);

  // Notes on the sheet:
  //   INPUTS to your circuit
  //   contents of rom_1 (hex, n*v repeats v):
  //   1001 1401 1601 1081 1481 1581 1101 1201 1281 1681 1301 1381 41 41 41 1041 10c1 1141 1241 12c1 16c1
  //   1341 13c1 2842 2842 2842 4*2064 2074 2074 1067 17e7 2069 2041
  //   ROM FOR CONTROL LOGIC
  //   DON'T CHANGE THE LOCATIONS OF THE INPUTS AND OUTPUTS!
  //   This is only if you choose to do the ROM option
  //   OUTPUT from your circuit
  //   Reminder: If using ROM, use combinational logic for PCSel
endmodule
