// Logisim project cpu.circ as structural Verilog: 1 circuit, main circuit cpu
module cpu (
  input  clk,
  input  [31:0] Instruction,
  input  [31:0] MemReadData,
  output [31:0] MemAddress,
  output [31:0] ProgramCounter,
  output [31:0] ra,
  output [31:0] sp,
  output [31:0] t0,
  output [31:0] t1,
  output [31:0] t2,
  output [31:0] s0,
  output [31:0] s1,
  output [31:0] a0,
  output [3:0] MemWriteMask,
  output [31:0] MemWriteData
);

  wire branch_comp_1_breq, branch_comp_1_brlt, BrUn, control_logic_1_asel, control_logic_1_bsel, MemWEn,
       PCSel, RegWEn;
  wire [1:0] WBSel;
  wire [2:0] ImmSel;
  wire [3:0] control_logic_1_alusel;
  wire [31:0] A, adder_1_out, adder_2_out, B, immediate, LoadDatatoRegister, multiplexer_1_out,
       multiplexer_2_out, multiplexer_3_out, multiplexer_4_out, Other, PipelinedInstruction,
       PipelinedProgramCounter, WriteDataResult;

  Adder #(.width(32)) adder_1 (.a(ProgramCounter), .b(32'h4), .out(adder_1_out));  // open: cin, cout
  Register #(.width(32)) register_1 (.D(adder_1_out), .clk(clk), .Q(Other));  // open: en, clr
  Register #(.width(32)) PC (.D(multiplexer_1_out), .clk(clk), .Q(ProgramCounter));  // open: en, clr
  Multiplexer #(.width(32)) multiplexer_1 (.in0(adder_1_out), .in1(MemAddress), .out(multiplexer_1_out), .sel(PCSel));
  Multiplexer #(.width(32)) multiplexer_2 (.in0(Instruction), .in1(32'h13), .out(multiplexer_2_out), .sel(PCSel));
  Register #(.width(32)) register_2 (.D(multiplexer_2_out), .clk(clk), .Q(PipelinedInstruction));  // open: en, clr
  Register #(.width(32)) register_3 (.D(ProgramCounter), .clk(clk), .Q(PipelinedProgramCounter));  // open: en, clr
  control_logic control_logic_1 (
    .Instruction(PipelinedInstruction), .BrEq(branch_comp_1_breq), .BrLt(branch_comp_1_brlt), .PCSel(PCSel),
    .RegWEn(RegWEn), .ImmSel(ImmSel), .BrUn(BrUn), .ASel(control_logic_1_asel), .BSel(control_logic_1_bsel),
    .ALUSel(control_logic_1_alusel), .MemWEn(MemWEn), .WBSel(WBSel));
  imm_gen imm_gen_1 (.Instruction(PipelinedInstruction), .ImmSel(ImmSel), .Immediate(immediate));
  regfile regfile_1 (
    .ReadIndex1(PipelinedInstruction[19:15]), .ReadIndex2(PipelinedInstruction[24:20]),
    .WriteIndex(PipelinedInstruction[11:7]), .WriteData(WriteDataResult), .RegWEn(RegWEn), .clk(clk),
    .ra(ra), .sp(sp), .t0(t0), .t1(t1), .t2(t2), .s0(s0), .s1(s1), .a0(a0), .ReadData1(A), .ReadData2(B));
  branch_comp branch_comp_1 (
    .BrData1(A), .BrData2(B), .BrUn(BrUn), .BrEq(branch_comp_1_breq), .BrLt(branch_comp_1_brlt));
  Multiplexer #(.width(32)) multiplexer_3 (
    .in0(A), .in1(PipelinedProgramCounter), .out(multiplexer_3_out), .sel(control_logic_1_asel));
  Multiplexer #(.width(32)) multiplexer_4 (
    .in0(B), .in1(immediate), .out(multiplexer_4_out), .sel(control_logic_1_bsel));
  alu alu_1 (.A(multiplexer_3_out), .B(multiplexer_4_out), .ALUSel(control_logic_1_alusel), .ALUResult(MemAddress));
  Adder #(.width(32)) adder_2 (.a(PipelinedProgramCounter), .b(32'h4), .out(adder_2_out));  // open: cin, cout
  Multiplexer #(.select(2), .width(32)) multiplexer_5 (
    .in0(LoadDatatoRegister), .in1(MemAddress), .in2(adder_2_out), .out(WriteDataResult), .sel(WBSel));  // open: in3
  partial_store partial_store_1 (
    .Instruction(PipelinedInstruction), .MemAddress(MemAddress), .DataFromReg(B), .MemWEn(MemWEn),
    .MemWriteMask(MemWriteMask), .DataToMem(MemWriteData));
  partial_load partial_load_1 (
    .Instruction(PipelinedInstruction), .MemAddress(MemAddress), .DataFromMem(MemReadData),
    .DataToReg(LoadDatatoRegister));

  // Other names for the same wires on the sheet: WriteIndex[4:0] = PipelinedInstruction[11:7];
  //   ReadIndex1[4:0] = PipelinedInstruction[19:15]; ReadIndex2[4:0] = PipelinedInstruction[24:20];
  //   WriteData[31:0] = MemAddress

  // Notes on the sheet:
  //   To IMEM
  //   IMEM (do **NOT** move this)
  //   From IMEM
  //   Inputs/Outputs for testing. Do **NOT** move these.
  //   To DMEM
  //   DMEM (do **NOT** move this)
  //   From DMEM
endmodule
