// Logisim project imm-gen.circ as structural Verilog: 1 circuit, main circuit imm_gen
module imm_gen (
  input  [31:0] Instruction,
  input  [2:0] ImmSel,
  output [31:0] Immediate
);

  wire [31:0] BImmediate, IImmediate, JImmediate, SImmediate, UImmediate;

  Multiplexer #(.select(3), .width(32)) multiplexer_1 (
    .in0(IImmediate), .in1(SImmediate), .in2(BImmediate), .in3(UImmediate), .in4(JImmediate),
    .out(Immediate), .sel(ImmSel));  // open: in5, in6, in7
  assign IImmediate = {{20{Instruction[31]}}, Instruction[31:20]};  // Bit_Extender bit_extender_1
  assign JImmediate = {{11{Instruction[31]}}, {Instruction[31], Instruction[19:12], Instruction[20], Instruction[30:21], 1'b0}};  // Bit_Extender bit_extender_2
  assign SImmediate = {{20{Instruction[31]}}, {Instruction[31:25], Instruction[11:7]}};  // Bit_Extender bit_extender_3
  Bit_Extender #(.in_width(32), .out_width(32)) bit_extender_4 (
    .in({Instruction[31:12], {12{1'b0}}}), .out(UImmediate));
  assign BImmediate = {{19{Instruction[31]}}, {Instruction[31], Instruction[7], Instruction[30:25], Instruction[11:8], 1'b0}};  // Bit_Extender bit_extender_5

  // Notes on the sheet:
  //   INPUTS to your circuit
  //   DON'T CHANGE THE LOCATIONS OF THE INPUTS AND OUTPUTS!
  //   OUTPUT from your circuit
endmodule
