// Logisim project regfile.circ as structural Verilog: 1 circuit, main circuit regfile
module regfile (
  input  [4:0] ReadIndex1,
  input  [4:0] ReadIndex2,
  input  [4:0] WriteIndex,
  input  [31:0] WriteData,
  input  RegWEn,
  input  clk,
  output [31:0] ra,
  output [31:0] sp,
  output [31:0] t0,
  output [31:0] t1,
  output [31:0] t2,
  output [31:0] s0,
  output [31:0] s1,
  output [31:0] a0,
  output [31:0] ReadData1,
  output [31:0] ReadData2
);

  wire wx0, wx1, wx2, wx3, wx4, wx5, wx6, wx7, wx8, wx9, wx10, wx11, wx12, wx13, wx14, wx15, wx16, wx17,
       wx18, wx19, wx20, wx21, wx22, wx23, wx24, wx25, wx26, wx27, wx28, wx29, wx30, wx31;
  wire [31:0] x0, x3, x4, x11, x12, x13, x14, x15, x16, x17, x18, x19, x20, x21, x22, x23, x24, x25, x26,
       x27, x28, x29, x30, x31;

  Demultiplexer #(.select(5)) demultiplexer_1 (
    .out0(wx0), .out1(wx1), .out2(wx2), .out3(wx3), .out4(wx4), .out5(wx5), .out6(wx6), .out7(wx7),
    .out8(wx8), .out9(wx9), .out10(wx10), .out11(wx11), .out12(wx12), .out13(wx13), .out14(wx14),
    .out15(wx15), .out16(wx16), .out17(wx17), .out18(wx18), .out19(wx19), .out20(wx20), .out21(wx21),
    .out22(wx22), .out23(wx23), .out24(wx24), .out25(wx25), .out26(wx26), .out27(wx27), .out28(wx28),
    .out29(wx29), .out30(wx30), .out31(wx31), .in(RegWEn), .sel(WriteIndex));
  Register #(.width(32)) register_1 (.D({32{1'b0}}), .en(1'b0), .clk(clk), .Q(x0));  // open: clr
  Register #(.width(32)) register_2 (.D(WriteData), .en(wx2), .clk(clk), .Q(sp));  // open: clr
  Register #(.width(32)) register_3 (.D(WriteData), .en(wx4), .clk(clk), .Q(x4));  // open: clr
  Register #(.width(32)) register_4 (.D(WriteData), .en(wx6), .clk(clk), .Q(t1));  // open: clr
  Register #(.width(32)) register_5 (.D(WriteData), .en(wx8), .clk(clk), .Q(s0));  // open: clr
  Register #(.width(32)) register_6 (.D(WriteData), .en(wx10), .clk(clk), .Q(a0));  // open: clr
  Register #(.width(32)) register_7 (.D(WriteData), .en(wx12), .clk(clk), .Q(x12));  // open: clr
  Register #(.width(32)) register_8 (.D(WriteData), .en(wx14), .clk(clk), .Q(x14));  // open: clr
  Register #(.width(32)) register_9 (.D(WriteData), .en(wx16), .clk(clk), .Q(x16));  // open: clr
  Register #(.width(32)) register_10 (.D(WriteData), .en(wx18), .clk(clk), .Q(x18));  // open: clr
  Register #(.width(32)) register_11 (.D(WriteData), .en(wx20), .clk(clk), .Q(x20));  // open: clr
  Register #(.width(32)) register_12 (.D(WriteData), .en(wx22), .clk(clk), .Q(x22));  // open: clr
  Register #(.width(32)) register_13 (.D(WriteData), .en(wx24), .clk(clk), .Q(x24));  // open: clr
  Register #(.width(32)) register_14 (.D(WriteData), .en(wx26), .clk(clk), .Q(x26));  // open: clr
  Register #(.width(32)) register_15 (.D(WriteData), .en(wx28), .clk(clk), .Q(x28));  // open: clr
  Register #(.width(32)) register_16 (.D(WriteData), .en(wx30), .clk(clk), .Q(x30));  // open: clr
  Register #(.width(32)) register_17 (.D(WriteData), .en(wx1), .clk(clk), .Q(ra));  // open: clr
  Register #(.width(32)) register_18 (.D(WriteData), .en(wx3), .clk(clk), .Q(x3));  // open: clr
  Register #(.width(32)) register_19 (.D(WriteData), .en(wx5), .clk(clk), .Q(t0));  // open: clr
  Register #(.width(32)) register_20 (.D(WriteData), .en(wx7), .clk(clk), .Q(t2));  // open: clr
  Register #(.width(32)) register_21 (.D(WriteData), .en(wx9), .clk(clk), .Q(s1));  // open: clr
  Register #(.width(32)) register_22 (.D(WriteData), .en(wx11), .clk(clk), .Q(x11));  // open: clr
  Register #(.width(32)) register_23 (.D(WriteData), .en(wx13), .clk(clk), .Q(x13));  // open: clr
  Register #(.width(32)) register_24 (.D(WriteData), .en(wx15), .clk(clk), .Q(x15));  // open: clr
  Register #(.width(32)) register_25 (.D(WriteData), .en(wx17), .clk(clk), .Q(x17));  // open: clr
  Register #(.width(32)) register_26 (.D(WriteData), .en(wx19), .clk(clk), .Q(x19));  // open: clr
  Register #(.width(32)) register_27 (.D(WriteData), .en(wx21), .clk(clk), .Q(x21));  // open: clr
  Register #(.width(32)) register_28 (.D(WriteData), .en(wx23), .clk(clk), .Q(x23));  // open: clr
  Register #(.width(32)) register_29 (.D(WriteData), .en(wx25), .clk(clk), .Q(x25));  // open: clr
  Register #(.width(32)) register_30 (.D(WriteData), .en(wx27), .clk(clk), .Q(x27));  // open: clr
  Register #(.width(32)) register_31 (.D(WriteData), .en(wx29), .clk(clk), .Q(x29));  // open: clr
  Register #(.width(32)) register_32 (.D(WriteData), .en(wx31), .clk(clk), .Q(x31));  // open: clr
  Multiplexer #(.select(5), .width(32)) multiplexer_1 (
    .in0(x0), .in1(ra), .in2(sp), .in3(x3), .in4(x4), .in5(t0), .in6(t1), .in7(t2), .in8(s0), .in9(s1),
    .in10(a0), .in11(x11), .in12(x12), .in13(x13), .in14(x14), .in15(x15), .in16(x16), .in17(x17),
    .in18(x18), .in19(x19), .in20(x20), .in21(x21), .in22(x22), .in23(x23), .in24(x24), .in25(x25),
    .in26(x26), .in27(x27), .in28(x28), .in29(x29), .in30(x30), .in31(x31), .out(ReadData1), .sel(ReadIndex1));
  Multiplexer #(.select(5), .width(32)) multiplexer_2 (
    .in0(x0), .in1(ra), .in2(sp), .in3(x3), .in4(x4), .in5(t0), .in6(t1), .in7(t2), .in8(s0), .in9(s1),
    .in10(a0), .in11(x11), .in12(x12), .in13(x13), .in14(x14), .in15(x15), .in16(x16), .in17(x17),
    .in18(x18), .in19(x19), .in20(x20), .in21(x21), .in22(x22), .in23(x23), .in24(x24), .in25(x25),
    .in26(x26), .in27(x27), .in28(x28), .in29(x29), .in30(x30), .in31(x31), .out(ReadData2), .sel(ReadIndex2));

  // Notes on the sheet:
  //   INPUTS to your circuit
  //   DON'T CHANGE THE LOCATIONS OF THE INPUTS AND OUTPUTS!
  //   These are DEBUG/TEST outputs from your circuit.
  //   OUTPUTS from your circuit
endmodule
